// Logisim project ex1.circ as structural Verilog: 1 circuit, main circuit generate_immediate
module generate_immediate (
  input  [31:0] INSTRUCTION,
  output [31:0] IMMEDIATE
);

  wire [31:0] B, I, J, U;

  assign I = {{20{INSTRUCTION[31]}}, INSTRUCTION[31:20]};  // Bit_Extender bit_extender_1
  assign IMMEDIATE = {{20{INSTRUCTION[31]}}, {INSTRUCTION[31:25], INSTRUCTION[11:7]}};  // Bit_Extender bit_extender_2
  assign U = {{12{INSTRUCTION[31]}}, INSTRUCTION[31:12]};  // Bit_Extender bit_extender_3
  assign B = {{19{INSTRUCTION[31]}}, {INSTRUCTION[31], INSTRUCTION[11], INSTRUCTION[30:25], INSTRUCTION[10:7], 1'b0}};  // Bit_Extender bit_extender_4
  assign J = {{11{INSTRUCTION[31]}}, {INSTRUCTION[31], INSTRUCTION[19:12], INSTRUCTION[20], INSTRUCTION[30:21], 1'b0}};  // Bit_Extender bit_extender_5

  // Other names for the same wires on the sheet: A[31:0] = INSTRUCTION; S[31:0] = IMMEDIATE
endmodule
