// Logisim project ex2.circ as structural Verilog: 1 circuit, main circuit compute_BrUn
module compute_BrUn (
  input  [31:0] INSTRUCTION,
  output BrUn
);

  Multiplexer #(.select(3)) multiplexer_1 (
    .in0(1'b0), .in1(1'b0), .in2(1'b0), .in3(1'b0), .in4(1'b0), .in5(1'b0), .in6(1'b1), .in7(1'b1),
    .out(BrUn), .sel(INSTRUCTION[14:12]));

  // Other names for the same wires on the sheet: A[31:0] = INSTRUCTION; B[2:0] = INSTRUCTION[14:12]
endmodule
