// Logisim project ex4.circ as structural Verilog: 1 circuit, main circuit pipelined
module pipelined (
  input  [7:0] in1,
  input  [7:0] in2,
  input  CLK,
  output [7:0] out1
);

  wire [7:0] Add, D, Mul;

  Register register_1 (.D(Mul), .clk(CLK), .Q(D));  // open: en, clr
  Register register_2 (.D(Add), .clk(CLK), .Q(out1));  // open: en, clr
  Adder adder_1 (.a(D), .b(out1), .out(Add));  // open: cin, cout
  Multiplier multiplier_1 (.a(in1), .b(in2), .out(Mul));  // open: cin, cout

  // Other names for the same wires on the sheet: A[7:0] = in1; B[7:0] = in2; C = CLK; E[7:0] = out1
endmodule
