// Logisim project ex5.circ as structural Verilog: 1 circuit, main circuit num_checker
module num_checker (
  input  [31:0] num,
  input  clk,
  output is_odd,
  output is_even,
  output is_zero,
  output greater_than_fifteen,
  output five_or_ten
);

  wire and_1_out, and_2_out, comparator_5_eq, comparator_6_eq, comparator_7_eq, comparator_8_eq;
  wire [15:0] adder_1_out, register_1_q;

  Adder #(.width(16)) adder_1 (.a(register_1_q), .b(16'h1), .out(adder_1_out));  // open: cin, cout
  Register #(.width(16)) register_1 (.D(adder_1_out), .en(1'b1), .clk(clk), .Q(register_1_q));  // open: clr
  Comparator #(.width(1)) comparator_1 (.a(num[0]), .b(1'b0), .eq(is_odd));  // open: gt, lt
  Comparator #(.width(1)) comparator_2 (.a(num[0]), .b(1'b1), .eq(is_even));  // open: gt, lt
  Comparator #(.width(32)) comparator_3 (.a(num), .b({32{1'b0}}), .eq(is_zero));  // open: gt, lt
  Comparator #(.width(28)) comparator_4 (.a(num[31:4]), .b({28{1'b0}}), .lt(greater_than_fifteen));  // open: gt, eq
  Comparator #(.width(3)) comparator_5 (.a(num[2:0]), .b(3'b111), .eq(comparator_5_eq));  // open: gt, lt
  Comparator #(.width(29)) comparator_6 (.a(num[31:3]), .b({29{1'b0}}), .eq(comparator_6_eq));  // open: gt, lt
  Comparator #(.width(2)) comparator_7 (.a({num[3], num[1]}), .b(2'b00), .eq(comparator_7_eq));  // open: gt, lt
  Comparator #(.width(30)) comparator_8 (
    .a({num[31:4], num[2], num[0]}), .b({30{1'b0}}), .eq(comparator_8_eq));  // open: gt, lt
  and and_1 (and_1_out, comparator_5_eq, comparator_6_eq);
  and and_2 (and_2_out, comparator_7_eq, comparator_8_eq);
  or or_1 (five_or_ten, and_1_out, and_2_out);

  // Other names for the same wires on the sheet: bit_zero = num[0]; bits_five[2:0] = num[2:0];
  //   ten_rest_zero[29:0] = {num[31:4], num[2], num[0]}; bits_ten[1:0] = {num[3], num[1]};
  //   five_rest_zero[28:0] = num[31:3]; bits_15[27:0] = num[31:4]

  // Notes on the sheet:
  //   num_cycles
endmodule
